# Fritzing sketch AtariPaddles (saved by Fritzing 1.0.1rc)
breadboards: 1

parts:
  Part2 = Arduino Micro (Rev3)
  S1 = Round Pushbutton
  S2 = Round Pushbutton
  R1 = Rotary Potentiometer (Large) [maximum_resistance=100kΩ knob_status=50% package=THT]
  R2 = Rotary Potentiometer (Large) [maximum_resistance=100kΩ knob_status=50% package=THT]
  ATARI_MALE = DB9 Connector [package=db9]
  ATARI_PADDLES = DB9 Connector [package=db9]
  LED1 = LED - 5mm [color="Red (633nm)" current=0.030 package="5 mm [THT]"]
  LED2 = LED - 5mm [color="Red (633nm)" current=0.030 package="5 mm [THT]"]
  LED3 = LED - 5mm [color="Red (633nm)" current=0.030 package="5 mm [THT]"]
  LED4 = LED - 5mm [color="Red (633nm)" current=0.030 package="5 mm [THT]"]
  R3 = Resistor [tolerance=±5% resistance=220 package="2010 [SMD]"]
  R4 = Resistor [tolerance=±5% resistance=220 package="2010 [SMD]"]
  R5 = Resistor [tolerance=±5% resistance=220 package="2010 [SMD]"]
  R6 = Resistor [tolerance=±5% resistance=220 package="2010 [SMD]"]

nets:
  N1: Part2.GND, R3.Pin_1, R4.Pin_1, R5.Pin_1, R6.Pin_1
  N2: Part2.D4_PWM/A6, LED4.anode
  N3: Part2.D6_PWM/A7, LED1.anode
  N4: Part2.D10_PWM/A10, ATARI_MALE.4
  N5: Part2.D11_PWM, LED2.anode
  N6: Part2.D12_PWM/A11, ATARI_MALE.3
  N7: Part2.5V, ATARI_MALE.7
  N8: Part2.A1, ATARI_MALE.9
  N9: Part2.A0, ATARI_MALE.8
  N10: Part2.D13_PWM, LED3.anode
  N11: S1.leg0, ATARI_PADDLES.4
  N12: S1.leg1, S2.leg1, ATARI_PADDLES.8
  N13: S2.leg0, ATARI_PADDLES.3
  N14: R1.leg1, R2.leg1, ATARI_PADDLES.7
  N15: R1.wiper, ATARI_PADDLES.9
  N16: R2.wiper, ATARI_PADDLES.5
  N17: LED1.cathode, R6.Pin_0
  N18: LED2.cathode, R4.Pin_0
  N19: LED3.cathode, R3.Pin_0
  N20: LED4.cathode, R5.Pin_0
