# Fritzing sketch AtariPaddles3 (saved by Fritzing 1.0.1rc)
breadboards: 1

parts:
  Part2 = Arduino Micro (Rev3)  # not connected
  S1 = Round Pushbutton
  S2 = Round Pushbutton
  R1 = Rotary Potentiometer (Large) [maximum_resistance=100kΩ knob_status=50% package=THT]
  R2 = Rotary Potentiometer (Large) [maximum_resistance=100kΩ knob_status=50% package=THT]
  ATARI_MALE = DB9 Connector [package=db9]
  ATARI_PADDLES = DB9 Connector [package=db9]
  LED1 = LED - 5mm [color="Red (633nm)" current=0.030 package="5 mm [THT]"]
  LED2 = LED - 5mm [color="Red (633nm)" current=0.030 package="5 mm [THT]"]
  LED3 = LED - 5mm [color="Red (633nm)" current=0.030 package="5 mm [THT]"]
  LED4 = LED - 5mm [color="Red (633nm)" current=0.030 package="5 mm [THT]"]
  R3 = Resistor [tolerance=±5% resistance=220 package="2010 [SMD]"]
  R5 = Resistor [tolerance=±5% resistance=220 package="2010 [SMD]"]
  R6 = Resistor [tolerance=±5% resistance=220 package="2010 [SMD]"]
  J1 = Dagu DGServo 9g header (male) [package=THT]
  J2 = Dagu DGServo 9g header (male) [package=THT]
  R4 = Resistor [tolerance=±5% resistance=220 package="2010 [SMD]"]
  R7 = Resistor [tolerance=±5% resistance=220 package="2010 [SMD]"]
  R8 = Resistor [tolerance=±5% resistance=220 package="2010 [SMD]"]
  R10 = Resistor [tolerance=±5% resistance=470 package="2010 [SMD]"]
  R9 = Resistor [tolerance=±5% resistance=470 package=THT]

nets (from the breadboard view):
  N1: S1.leg0, ATARI_PADDLES.4
  N2: S1.leg1, S2.leg1, ATARI_PADDLES.8
  N3: S2.leg0, ATARI_PADDLES.3
  N4: R1.leg1, R2.leg1, ATARI_PADDLES.7
  N5: R1.wiper, ATARI_PADDLES.9
  N6: R2.wiper, ATARI_PADDLES.5
  N7: ATARI_MALE.3, J1.pulse, R7.Pin_1
  N8: ATARI_MALE.4, J1.Vcc, R8.Pin_1
  N9: ATARI_MALE.5, J1.gnd, R10.Pin_0
  N10: ATARI_MALE.7, ATARI_MALE.8, J2.Vcc, J2.pulse
  N11: ATARI_MALE.9, J2.gnd, R9.Pin_0
  N12: LED1.cathode, R6.Pin_0
  N13: LED2.cathode, R4.Pin_0
  N14: LED3.cathode, R3.Pin_0
  N15: LED4.cathode, R5.Pin_0
  N16: R3.Pin_1, R5.Pin_1, R6.Pin_1, R4.Pin_1, R10.Pin_1, R9.Pin_1

notes:
  3-Button right
  4-Button Left
  5-Analog Left
  7-GND pin 5,9
  8-GND pin 3,4
  9-AnalogRight
  D5432
  BACK VIEW
  5 4 3 2 1
  9 8 7 6
  987 543
  A01-Paddle
  LED
  Pin=2345
  D23 = Fire Button
  D45 = Paddle PWM
  34 Button 8GND
  59 Wiper 7GND
